# Fritzing sketch gioco delle forme circuito (saved by Fritzing 0.9.3b)

parts:
  BAT1 = 18650 battery holder [package=battery-18650-kit]
  BAT2 = 18650 battery holder [package=battery-18650-kit]
  U1 = LM2596 step down module
  Componente1 = Arduino Mega 2560 (Rev3)
  DFPlayer_Mini1 = DFPlayer MINI [package="DIP (Dual Inline) [THT]"]
  led_forma1(1) = RGB LED - (4 legs) [package="5 mm [THT]"]
  Q1 = TRANSISTOR_NPN [package=to-92-ammo]
  SPKR1 = Loudspeaker
  Q2 = TRANSISTOR_NPN [package=to-92-ammo]
  Q3 = TRANSISTOR_NPN [package=to-92-ammo]
  S1 = SPST Switch [package=ayz0202]
  R1 = Resistor [tolerance=±5% resistance=1k package=THT]
  R2 = Resistor [tolerance=±5% resistance=1k package=THT]
  R3 = Resistor [tolerance=±5% resistance=1k package=THT]
  R4 = Resistor [tolerance=±5% resistance=1k package=THT]
  R5 = Resistor [tolerance=±5% resistance=1k package=THT]
  R6 = Resistor [tolerance=±5% resistance=1k package=THT]
  R7 = Resistor [tolerance=±5% resistance=1k package=THT]
  R8 = Resistor [tolerance=±5% resistance=1k package=THT]
  R9 = Resistor [tolerance=±5% resistance=1k package=THT]
  R10 = Resistor [tolerance=±5% resistance=1k package=THT]
  led_forma1(2) = RGB LED - (4 legs) [package="5 mm [THT]"]
  led_forma1(3) = RGB LED - (4 legs) [package="5 mm [THT]"]
  LED2 = RGB LED - (4 legs) [package="5 mm [THT]"]
  Part1 = KY-003 Hall Magnetic Sensor Module [package="Breakout board"]

nets:
  N1: BAT1.+, BAT2.-
  GND: BAT1.-, U1.IN-, U1.OUT-, Componente1.GND, DFPlayer_Mini1.GND, Q1.E, Q2.E, Q3.E, Part1.-
  N2: BAT2.+, S1.P
  N3: U1.IN+, Componente1.VIN, S1.S
  VCC: U1.OUT+, DFPlayer_Mini1.VCC, led_forma1(1).common_anode, led_forma1(2).common_anode, led_forma1(3).common_anode, LED2.common_anode, Part1.Vin
  N4: Componente1.A0, Part1.S
  N5: Componente1.D11_PWM, R10.Pin_0
  N6: Componente1.D10_PWM, DFPlayer_Mini1.TX
  N7: Componente1.D24, R4.Pin_0
  N8: Componente1.D25, R5.Pin_0
  N9: Componente1.D26, R6.Pin_0
  N10: Componente1.D45, R9.Pin_0
  N11: Componente1.D46, R7.Pin_0
  N12: Componente1.D47, R8.Pin_0
  N13: DFPlayer_Mini1.RX, R10.Pin_1
  N14: DFPlayer_Mini1.SPK1, SPKR1.pin2
  N15: DFPlayer_Mini1.SPK2, SPKR1.pin1
  N16: led_forma1(1).red_cathode, R1.Pin_1, led_forma1(2).red_cathode, led_forma1(3).red_cathode
  N17: led_forma1(1).green_cathode, R2.Pin_1, led_forma1(2).green_cathode, led_forma1(3).green_cathode
  N18: led_forma1(1).blue_cathode, R3.Pin_1, led_forma1(2).blue_cathode, led_forma1(3).blue_cathode
  N19: Q1.B, R7.Pin_1
  N20: Q1.C, R1.Pin_0
  N21: Q2.B, R8.Pin_1
  N22: Q2.C, R2.Pin_0
  N23: Q3.B, R9.Pin_1
  N24: Q3.C, R3.Pin_0
  N25: R4.Pin_1, LED2.red_cathode
  N26: R5.Pin_1, LED2.green_cathode
  N27: R6.Pin_1, LED2.blue_cathode

custom parts:
  18650 battery holder: 18650 Battery Holder
  LM2596 step down module: LM2596 DC-DC step down power supply module 3 A.
  DFPlayer MINI: MP3 module by DFRobot.com for playing Music from an SD-Card. Supports WAV and MP3 files.
  KY-003 Hall Magnetic Sensor Module: KEYES KY-003 Arduino Hall Magnetic Sensor Module is a switch that will turn on/off in the presence of a magnetic field.
